# Fritzing sketch ProximitySensorBack (saved by Fritzing 0.9.3b)
breadboards: 1

parts:
  Back_Right = hc-sr04
  Back_Left = hc-sr04
  BreakSignal = LED - 3mm [color="Red (633nm)" package="3 mm [THT]"]
  Part1 = Arduino Mega 2560 (Rev3)

nets:
  VCC: Back_Right.VCC, Back_Left.VCC, Part1.3V3
  N1: Back_Right.Trig, Part1.D13_PWM
  N2: Back_Right.Echo, Part1.D12_PWM
  GND: Back_Right.GND, Back_Left.GND, BreakSignal.anode, Part1.GND
  N3: Back_Left.Trig, Part1.D9_PWM
  N4: Back_Left.Echo, Part1.D8_PWM
  N5: BreakSignal.cathode, Part1.D5_PWM

// code stored in the sketch: Front_Sensors.ino




long duration;


int distance;





/*****************************************************************


Takes data from the sensors


INPUT: Echo and trig pin of the sensors


OUTPUT: Distance of detected object


*****************************************************************/


int sensor(int trigPin, int echoPin)


{


digitalWrite(trigPin, LOW);


delayMicroseconds(2);


digitalWrite(trigPin, HIGH);


delayMicroseconds(10);


digitalWrite(trigPin,LOW);





duration = pulseIn(echoPin, HIGH);





distance = duration * 0.034/2;





return distance;





}





const int fTrigPin = 11;


const int fEchoPin = 10;


const int frTrigPin = 13;


const int frEchoPin = 12;


const int flTrigPin = 9;


const int flEchoPin = 8;


const int brakeSignal = 5;





void setup()


{


pinMode(fTrigPin, OUTPUT);


pinMode(fEchoPin, INPUT);


pinMode(frTrigPin, OUTPUT);


pinMode(frEchoPin, INPUT);


pinMode(flTrigPin, OUTPUT);


pinMode(flEchoPin, INPUT);


pinMode(brakeSignal, OUTPUT);


Serial.begin(9600); 


}








int fDistance,frDistance, flDistance;





void loop() {


frDistance = sensor (frTrigPin, frEchoPin);


fDistance = sensor(fTrigPin, fEchoPin);


flDistance = sensor(flTrigPin, flEchoPin);





if ((frDistance < 200) && (frDistance != 0)) //Check if an object is detected by the front sensor


{


digitalWrite(brakeSignal, HIGH);


Serial.print("Object Detected - Front Right - ");


Serial.print(frDistance);


Serial.print (" cm");


Serial.println();


}





else if ((fDistance < 200) && (fDistance != 0))


{


digitalWrite(brakeSignal, HIGH);


Serial.print("Object Detected - Front - ");


Serial.print(fDistance);


Serial.print(" cm");


Serial.println();


}





else if ((flDistance < 200) && (flDistance != 0))


{


digitalWrite(brakeSignal, HIGH);


Serial.print("Object Detected - Front Left - ");


Serial.print(flDistance);


Serial.print( " cm");


Serial.println();


}





else


{


digitalWrite(brakeSignal, LOW);


} 


}
