# Fritzing sketch Shifter wiring (saved by Fritzing 0.9.3b)
breadboards: 1

parts:
  Part1 = Arduino Mega ADK (Rev3)
  S1 = SWITCH-MOMENTARY-2 [package=tactile-switch-1101ne]
  S2 = SWITCH-MOMENTARY-2 [package=tactile-switch-1101ne]
  M1 = Stepper Motor - Bipolar
  VCC1 = 4 x AAA Battery Mount
  S3 = H-Bridge with L298N
  R1 = Resistor [tolerance=±5% resistance=10k package="0603 [SMD]"]
  R2 = Resistor [tolerance=±5% resistance=10k package="0603 [SMD]"]
  R3 = Resistor [tolerance=±5% resistance=10k package="0603 [SMD]"]
  S4 = Pushbutton [part_number=Forward package="[THT]"]
  S5 = Pushbutton [part_number=Reverse package="[THT]"]
  S6 = Pushbutton [part_number=Neutral package="[THT]"]

nets:
  5V: Part1.5V, VCC1.+, S3.5V, S4.Pin_3, S4.Pin_4, S5.Pin_3, S5.Pin_4, S6.Pin_3, S6.Pin_4
  GND: Part1.GND, S1.1, S2.1, VCC1.-, S3.GND, R1.Pin_0, R2.Pin_0, R3.Pin_0
  N1: Part1.D22, S3.IN1
  N2: Part1.D23, S3.IN2
  N3: Part1.D24, S3.IN3
  N4: Part1.D25, S3.IN4
  N5: Part1.D26, R1.Pin_1, S4.Pin_1, S4.Pin_2
  N6: Part1.D27, R2.Pin_1, S5.Pin_1, S5.Pin_2
  N7: Part1.D28, S2.2
  N8: Part1.D29, S1.2
  N9: Part1.D30, R3.Pin_1, S6.Pin_1, S6.Pin_2
  N10: M1.A, S3.M1-01
  N11: M1.C, S3.M1-02
  N12: M1.B, S3.M2-02
  N13: M1.D, S3.M2-01
  N14: S3.ENA, S3.ENA-5V
  N15: S3.ENB, S3.ENB-5V

notes:
  gearSwitch
  reverseSwitf

custom parts:
  H-Bridge with L298N: h-bridge
